# Fritzing sketch stopwatch_tm1637 (saved by Fritzing 0.9.2b)
circuit board: 8.46667cm x 5.64444cm
breadboards: 1

parts:
  7SEG1 = 7-Segment LED I2C Backpack (red)
  Part1 = Arduino Pro Mini v13

nets:
  N1: 7SEG1.V+, Part1.VCC
  GND: 7SEG1.GND, Part1.GND
  N2: 7SEG1.SDA, Part1.D4
  N3: 7SEG1.SCL, Part1.D3_PWM

custom parts:
  7-Segment LED I2C Backpack (red): 4-digit, 7-segment LED Display with I2C Control
